# Fritzing sketch mosfet_not_step3 (saved by Fritzing 0.8.5b)
breadboards: 1

parts:
  LED1 = LED - 5mm [color="Green (555nm)" package="5 mm [THT]"]
  R1 = Resistor [tolerance=±5% resistance=10k package=THT]
  R2 = Resistor [tolerance=±5% resistance=150 package=THT]
  Q1 = PNP-Transistor [package="TO92 [THT]"]  # not connected
  S1 = Pushbutton (square 0.2") [package="[THT]"]

nets:
  N1: LED1.cathode, R2.Pin_1
  N2: LED1.anode, R1.Pin_1, S1.Pin_3, S1.Pin_4
  N3: R1.Pin_0, R2.Pin_0
  N4: S1.Pin_1, S1.Pin_2

custom parts:
  Pushbutton (square 0.2"): A generic 0.2" x 0.2" pushbutton.
