# Fritzing sketch mosfet_not_step4 (saved by Fritzing 0.8.5b)
breadboards: 1

parts:
  Q2 = NPN-Transistor [package="TO92 [THT]"]
  LED1 = LED - 5mm [color="Green (555nm)" package="5 mm [THT]"]
  Q1 = PNP-Transistor [package="TO92 [THT]"]
  S1 = Pushbutton (square 0.2") [package="[THT]"]
  R1 = Resistor [tolerance=±1% resistance=10k package=THT]
  R2 = Resistor [tolerance=±1% resistance=150 package=THT]

nets:
  N1: Q2.E, Q1.C
  N2: LED1.cathode, R2.Pin_1
  N3: LED1.anode, S1.Pin_3, S1.Pin_4, R1.Pin_1
  N4: S1.Pin_1, S1.Pin_2
  N5: R1.Pin_0, R2.Pin_0

custom parts:
  Pushbutton (square 0.2"): A generic 0.2" x 0.2" pushbutton.
