# Fritzing sketch mosfet_not_step6 (saved by Fritzing 0.8.5b)
breadboards: 1

parts:
  Q2 = NPN-Transistor [package="TO92 [THT]"]
  LED1 = LED - 5mm [color="Green (555nm)" package="5 mm [THT]"]
  R3 = Resistor [tolerance=±5% resistance=150 package=THT]
  R1 = Resistor [tolerance=±5% resistance=10k package=THT]
  Q1 = PNP-Transistor [package="TO92 [THT]"]
  LED2 = LED - 5mm [color="Green (555nm)" package="5 mm [THT]"]
  R2 = Resistor [tolerance=±5% resistance=150 package=THT]
  S1 = Pushbutton (square 0.2") [package="[THT]"]

nets:
  N1: Q2.E, Q1.C, LED2.anode
  N2: Q2.B, LED1.anode, R1.Pin_1, Q1.B, S1.Pin_3, S1.Pin_4
  N3: Q2.C, R3.Pin_0, R1.Pin_0, R2.Pin_0
  N4: LED1.cathode, R2.Pin_1
  N5: R3.Pin_1, LED2.cathode
  N6: Q1.E, S1.Pin_1, S1.Pin_2

custom parts:
  Pushbutton (square 0.2"): A generic 0.2" x 0.2" pushbutton.
