# Fritzing sketch capacitors-series (saved by Fritzing 0.8.7b)
breadboards: 1

parts:
  LED1 = LED - 5mm [color="Green (555nm)" package="5 mm [THT]"]
  S2 = Pushbutton (square 0.2") [package="[THT]"]
  R1 = Resistor [tolerance=±1% resistance=150 package=THT]
  LED2 = LED - 5mm [color="Green (555nm)" package="5 mm [THT]"]
  R2 = Resistor [tolerance=±1% resistance=150 package=THT]
  S1 = Pushbutton (square 0.2") [package="[THT]"]
  C1 = Electrolytic Capacitor [capacitance=1µF package="100 mil [THT, electrolytic]"]
  C2 = Electrolytic Capacitor [capacitance=1µF package="100 mil [THT, electrolytic]"]

nets:
  N1: LED1.cathode, R1.Pin_1
  N2: LED1.anode, S1.Pin_1, S1.Pin_2
  GND: S2.Pin_1, S2.Pin_2, C1.-
  N3: S2.Pin_3, S2.Pin_4, LED2.cathode
  N4: R1.Pin_0, R2.Pin_1, C2.+
  N5: LED2.anode, R2.Pin_0
  5V: S1.Pin_3, S1.Pin_4
  N6: C1.+, C2.-

custom parts:
  Pushbutton (square 0.2"): A generic 0.2" x 0.2" pushbutton.
